// Logisim project ALU_4_bit.circ as structural Verilog: 1 circuit, main circuit main
module main (
  input  B3,
  input  B2,
  input  B1,
  input  B0,
  input  A3,
  input  A2,
  input  A1,
  input  A0,
  input  S2,
  input  S1,
  input  Cin,
  output Z,
  output V,
  output S,
  output C,
  output Cout,
  output O3,
  output O2,
  output O1,
  output O0
);

  wire _23__6__s2, n7404_1__2__1y, n7408_1__3__1y, n7408_1__6__2y, n7408_1__8__3y, n7408_1__11__4y,
       n7408_2__3__1y, n7408_2__6__2y, n7408_2__8__3y, n7408_2__11__4y, n7408_3__3__1y, n7408_3__6__2y,
       n7408_3__8__3y, n7408_3__11__4y, n7432_1__3__1y, n7432_1__6__2y, n7432_1__8__3y, n7432_1__11__4y,
       n7432_2__3__1y, n7432_2__6__2y, n7432_2__8__3y, n7483_1__6__s2, n7483_1__14_cout, n7486_1__3__1y,
       n7486_1__6__2y, n7486_1__8__3y, n7486_1__11__4y;

  _7432 u_7432_1 (
    ._1__1A(n7404_1__2__1y), ._2__1B(n7486_1__11__4y), ._3__1Y(n7432_1__3__1y), ._4__2A(n7404_1__2__1y),
    ._5__2B(n7486_1__8__3y), ._6__2Y(n7432_1__6__2y), ._14__Vcc(1'b1), ._13__4B(n7404_1__2__1y),
    ._12__4A(n7486_1__3__1y), ._11__4Y(n7432_1__11__4y), ._10__3B(n7404_1__2__1y), ._9__3A(n7486_1__6__2y),
    ._8__3Y(n7432_1__8__3y));  // open: _7__GND
  _7408 u_7408_1 (
    ._1__1A(n7432_1__3__1y), ._2__1B(A1), ._3__1Y(n7408_1__3__1y), ._4__2A(n7432_1__6__2y), ._5__2B(A0),
    ._6__2Y(n7408_1__6__2y), ._14__Vcc(1'b1), ._13__4B(n7432_1__8__3y), ._12__4A(A2),
    ._11__4Y(n7408_1__11__4y), ._10__3B(n7404_1__2__1y), ._9__3A(Cin), ._8__3Y(n7408_1__8__3y));  // open: _7__GND
  _7486 u_7486_1 (
    ._1__1A(S2), ._2__1B(B3), ._3__1Y(n7486_1__3__1y), ._4__2A(S2), ._5__2B(B2), ._6__2Y(n7486_1__6__2y),
    ._14__Vcc(1'b1), ._13__4B(S2), ._12__4A(B1), ._11__4Y(n7486_1__11__4y), ._10__3B(S2), ._9__3A(B0),
    ._8__3Y(n7486_1__8__3y));  // open: _7__GND
  _7408 u_7408_2 (
    ._1__1A(B3), ._2__1B(S2), ._3__1Y(n7408_2__3__1y), ._4__2A(A3), ._5__2B(n7432_1__11__4y),
    ._6__2Y(n7408_2__6__2y), ._14__Vcc(1'b1), ._13__4B(n7404_1__2__1y), ._12__4A(n7483_1__6__s2),
    ._11__4Y(n7408_2__11__4y), ._10__3B(n7404_1__2__1y), ._9__3A(n7483_1__14_cout), ._8__3Y(n7408_2__8__3y));  // open: _7__GND
  _7483 u_7483_1 (
    ._1__A4(n7408_1__3__1y), ._3__A3(1'b1), ._4__B3(n7408_2__11__4y), ._5__Vcc(1'b1),
    ._6__S2(n7483_1__6__s2), ._7__B2(1'b0), ._8__A2(1'b0), ._16__B4(n7408_3__11__4y), ._15__S4(O1),
    ._14_Cout(n7483_1__14_cout), ._13__Cin(n7408_1__8__3y), ._12__GND(1'b0), ._11__B1(n7408_3__3__1y),
    ._10__A1(n7408_1__6__2y), ._9__S1(O0));  // open: _2__S3
  _7483 _23 (
    ._1__A4(n7408_2__6__2y), ._3__A3(1'b1), ._4__B3(n7408_3__6__2y), ._5__Vcc(1'b1), ._6__S2(_23__6__s2),
    ._7__B2(1'b0), ._8__A2(1'b0), ._16__B4(n7408_2__3__1y), ._15__S4(O3), ._14_Cout(C),
    ._13__Cin(n7408_2__8__3y), ._12__GND(1'b0), ._11__B1(n7408_3__8__3y), ._10__A1(n7408_1__11__4y),
    ._9__S1(O2));  // open: _2__S3
  _7486 u_7486_2 (
    ._1__1A(C), ._2__1B(_23__6__s2), ._3__1Y(V), ._7__GND(1'b0), ._14__Vcc(1'b1));  // open: _4__2A, _5__2B, _6__2Y, _13__4B, _12__4A, _11__4Y, _10__3B, _9__3A, _8__3Y
  _7432 u_7432_2 (
    ._1__1A(O0), ._2__1B(O1), ._3__1Y(n7432_2__3__1y), ._4__2A(n7432_2__3__1y), ._5__2B(O2),
    ._6__2Y(n7432_2__6__2y), ._7__GND(1'b0), ._14__Vcc(1'b1), ._10__3B(O3), ._9__3A(n7432_2__6__2y),
    ._8__3Y(n7432_2__8__3y));  // open: _13__4B, _12__4A, _11__4Y
  _7404 u_7404_1 (
    ._1__1A(S1), ._2__1Y(n7404_1__2__1y), ._7__GND(1'b0), ._14__Vcc(1'b1), ._13__6A(n7432_2__8__3y),
    ._12__6Y(Z));  // open: _3__2A, _4__2Y, _5__3A, _6__3Y, _11__5A, _10__5Y, _9__4A, _8__4Y
  _7408 u_7408_3 (
    ._1__1A(B0), ._2__1B(S2), ._3__1Y(n7408_3__3__1y), ._4__2A(n7404_1__2__1y), ._5__2B(_23__6__s2),
    ._6__2Y(n7408_3__6__2y), ._7__GND(1'b0), ._14__Vcc(1'b1), ._13__4B(S2), ._12__4A(B1),
    ._11__4Y(n7408_3__11__4y), ._10__3B(S2), ._9__3A(B2), ._8__3Y(n7408_3__8__3y));

  assign Cout = C;
  assign S = O3;

  // Notes on the sheet:
  //   z1
  //   c1
  //   c2
  //   z2
  //   c3
  //   z3
endmodule
