// Logisim project Group_3_Floating_point_addition.circ as structural Verilog: 9 circuits, main circuit main
module main (
  input  [31:0] X,
  input  [31:0] Y,
  output U,
  output O,
  output [31:0] Out
);

  Floating_point_adder floating_point_adder_1 (.X(X), .Y(Y), .Out(Out), .OVERFLOW(O), .UNDERFLOW(U));
endmodule

module comparator (
  input  [9:0] X,
  input  [9:0] Y,
  output X_Y,
  output [9:0] LARGER,
  output [4:0] DIFFERENCE
);

  wire ALU_2_n;
  wire [9:0] MUX_2_out, negator_1_out;
  wire [9:5] MUX_3_out;
  wire [15:0] ALU_alu_out;

  ALU_16_bit ALU (
    .ALU_A_IN({{6{1'b0}}, X}), .ALU_B_IN({{6{1'b0}}, Y}), .OP_CODE(3'b001), .ALU_OUT(ALU_alu_out), .N(X_Y));  // open: Z
  MUX_10_bit MUX (._0(X), ._1(Y), .SELECT(X_Y), .OUT(LARGER));
  Negator #(.width(10)) negator_1 (.in(ALU_alu_out[9:0]), .out(negator_1_out));
  MUX_10_bit MUX_2 (._0(ALU_alu_out[9:0]), ._1(negator_1_out), .SELECT(X_Y), .OUT(MUX_2_out));
  ALU_16_bit ALU_2 (
    .ALU_A_IN({{6{1'b0}}, MUX_2_out}), .ALU_B_IN(16'h1f), .OP_CODE(3'b001), .N(ALU_2_n));  // open: ALU_OUT, Z
  MUX_10_bit MUX_3 (._0(10'h1f), ._1(MUX_2_out), .SELECT(ALU_2_n), .OUT({MUX_3_out, DIFFERENCE}));

  // Notes on the sheet:
  //   finds diff
  //   finds larger
  //   makes diff pos if neg
  //   max shamt can be 11111
endmodule

module Sign_check (
  input  Sign,
  input  [31:0] Fraction,
  input  [9:0] Exponent,
  output [31:0] \output 
);

  wire bitfinder_1_found;
  wire [31:0] mux_32_bit_1_out_4, negator_1_out;

  BitFinder #(.width(10)) bitfinder_1 (.in(Exponent), .found(bitfinder_1_found));  // open: index
  Negator #(.width(32)) negator_1 (.in(Fraction), .out(negator_1_out));
  MUX_32_bit mux_32_bit_1 (._0(Fraction), ._1(negator_1_out), .S(Sign), .out_4(mux_32_bit_1_out_4));
  MUX_32_bit mux_32_bit_2 (._0({32{1'b0}}), ._1(mux_32_bit_1_out_4), .S(bitfinder_1_found), .out_4(\output ));
endmodule

module ALU_16_bit (
  input  [15:0] ALU_A_IN,
  input  [15:0] ALU_B_IN,
  input  [2:0] OP_CODE,
  output [15:0] ALU_OUT,
  output Z,
  output N
);

  wire adder_1_cout;
  wire [15:0] adder_1_out, and_1_out, multiplexer_1_out, multiplexer_2_out, multiplexer_3_out,
       multiplexer_4_out, not_1_out, or_1_out, shifter_1_out, shifter_2_out, subtractor_1_out, xor_1_out;

  Adder #(.width(16)) adder_1 (.a(ALU_A_IN), .b(ALU_B_IN), .out(adder_1_out), .cout(adder_1_cout));  // open: cin
  Subtractor #(.width(16)) subtractor_1 (
    .a(ALU_A_IN), .b(ALU_B_IN), .out(subtractor_1_out), .bin(adder_1_cout));  // open: bout
  assign and_1_out = ALU_A_IN & ALU_B_IN;  // AND_Gate and_1, 16 bits wide
  assign or_1_out = ALU_A_IN | ALU_B_IN;  // OR_Gate or_1, 16 bits wide
  assign not_1_out = ~ALU_A_IN;  // NOT_Gate not_1, 16 bits wide
  assign xor_1_out = ALU_A_IN ^ ALU_B_IN;  // XOR_Gate xor_1, 16 bits wide
  Shifter #(.width(16), .shift("rl")) shifter_1 (.in(ALU_A_IN), .\dist (4'b0001), .out(shifter_1_out));
  Shifter #(.width(16), .shift("rr")) shifter_2 (.in(ALU_A_IN), .\dist (4'b0001), .out(shifter_2_out));
  Multiplexer #(.width(16), .enable("false")) multiplexer_1 (
    .in0(adder_1_out), .in1(subtractor_1_out), .out(multiplexer_1_out), .sel(OP_CODE[0]));
  Multiplexer #(.width(16), .enable("false")) multiplexer_2 (
    .in0(and_1_out), .in1(or_1_out), .out(multiplexer_2_out), .sel(OP_CODE[0]));
  Multiplexer #(.width(16), .enable("false")) multiplexer_3 (
    .in0(not_1_out), .in1(xor_1_out), .out(multiplexer_3_out), .sel(OP_CODE[0]));
  Multiplexer #(.width(16), .enable("false")) multiplexer_4 (
    .in0(shifter_1_out), .in1(shifter_2_out), .out(multiplexer_4_out), .sel(OP_CODE[0]));
  nor nor_1 (Z, ALU_OUT[0], ALU_OUT[1], ALU_OUT[2], ALU_OUT[3], ALU_OUT[4], ALU_OUT[5], ALU_OUT[6], ALU_OUT[7], ALU_OUT[8], ALU_OUT[9], ALU_OUT[10], ALU_OUT[11], ALU_OUT[12], ALU_OUT[13], ALU_OUT[14], ALU_OUT[15]);
  Multiplexer #(.select(2), .width(16), .enable("false")) multiplexer_5 (
    .in0(multiplexer_1_out), .in1(multiplexer_2_out), .in2(multiplexer_3_out), .in3(multiplexer_4_out),
    .out(ALU_OUT), .sel(OP_CODE[2:1]));

  assign N = ALU_OUT[15];
endmodule

module MUX_10_bit (
  input  [9:0] _0,
  input  [9:0] _1,
  input  SELECT,
  output [9:0] OUT
);

  _74157 u_74157_1 (
    ._1__S(SELECT), ._2__A1(_0[0]), ._3__B1(_1[0]), ._4__Y1(OUT[0]), ._5__A2(_0[1]), ._6__B2(_1[1]),
    ._7__Y2(OUT[1]), ._15__G(1'b0), ._14__A4(_0[2]), ._13__B4(_1[2]), ._12__Y4(OUT[2]), ._11__A3(_0[3]),
    ._10__B3(_1[3]), ._9__Y3(OUT[3]));  // open: _8__GND, _16__Vcc
  _74157 u_74157_2 (
    ._1__S(SELECT), ._2__A1(_0[4]), ._3__B1(_1[4]), ._4__Y1(OUT[4]), ._5__A2(_0[5]), ._6__B2(_1[5]),
    ._7__Y2(OUT[5]), ._15__G(1'b0), ._14__A4(_0[7]), ._13__B4(_1[7]), ._12__Y4(OUT[7]), ._11__A3(_0[6]),
    ._10__B3(_1[6]), ._9__Y3(OUT[6]));  // open: _8__GND, _16__Vcc
  _74157 u_74157_3 (
    ._1__S(SELECT), ._2__A1(_0[8]), ._3__B1(_1[8]), ._4__Y1(OUT[8]), ._5__A2(_0[9]), ._6__B2(_1[9]),
    ._7__Y2(OUT[9]), ._15__G(1'b0));  // open: _8__GND, _16__Vcc, _14__A4, _13__B4, _12__Y4, _11__A3, _10__B3, _9__Y3
endmodule

module Normalizer (
  input  [31:0] Fraction,
  input  [9:0] Exponent,
  output [31:0] NORMALIZED_FRACTION,
  output [9:0] NORMALIZED_EXPONENT,
  output OVERFLOW,
  output UNDERFLOW
);

  wire alu_16_bit_1_n, alu_16_bit_1_z, bitfinder_1_found, n7408_1__6__2y;
  wire [0:0] COMP_with_29_x_y;
  wire [4:0] bitfinder_1_index, COMP_with_29_difference;
  wire [9:0] mux_10_bit_1_out;
  wire [15:0] alu_16_bit_1_alu_out;
  wire [31:0] shifter_1_out, shifter_2_out;

  BitFinder #(.width(32), .\type ("high1")) bitfinder_1 (
    .in(Fraction), .index(bitfinder_1_index), .found(bitfinder_1_found));
  MUX_10_bit mux_10_bit_1 (._0({10{1'b0}}), ._1(10'h1d), .SELECT(bitfinder_1_found), .OUT(mux_10_bit_1_out));
  comparator COMP_with_29 (
    .X({{5{1'b0}}, bitfinder_1_index}), .Y(mux_10_bit_1_out), .X_Y(COMP_with_29_x_y[0]),
    .DIFFERENCE(COMP_with_29_difference));  // open: LARGER
  Shifter #(.width(32), .shift("lr")) shifter_1 (.in(Fraction), .\dist (COMP_with_29_difference), .out(shifter_1_out));
  Shifter #(.width(32)) shifter_2 (.in(Fraction), .\dist (COMP_with_29_difference), .out(shifter_2_out));
  ALU_16_bit alu_16_bit_1 (
    .ALU_A_IN({{6{1'b0}}, Exponent}), .ALU_B_IN({{11{1'b0}}, COMP_with_29_difference}),
    .OP_CODE({2'b00, COMP_with_29_x_y[0]}), .ALU_OUT(alu_16_bit_1_alu_out), .Z(alu_16_bit_1_z),
    .N(alu_16_bit_1_n));
  _7408 u_7408_1 (
    ._4__2A(alu_16_bit_1_z), ._5__2B(bitfinder_1_found), ._6__2Y(n7408_1__6__2y));  // open: _1__1A, _2__1B, _3__1Y, _7__GND, _14__Vcc, _13__4B, _12__4A, _11__4Y, _10__3B, _9__3A, _8__3Y
  _7432 u_7432_1 (
    ._1__1A(n7408_1__6__2y), ._2__1B(alu_16_bit_1_n), ._3__1Y(UNDERFLOW));  // open: _4__2A, _5__2B, _6__2Y, _7__GND, _14__Vcc, _13__4B, _12__4A, _11__4Y, _10__3B, _9__3A, _8__3Y
  MUX_32_bit MUX (._0(shifter_1_out), ._1(shifter_2_out), .S(COMP_with_29_x_y[0]), .out_4(NORMALIZED_FRACTION));
  ALU_16_bit alu_16_bit_2 (
    .ALU_A_IN(16'h3fe), .ALU_B_IN(alu_16_bit_1_alu_out), .OP_CODE(3'b001), .N(OVERFLOW));  // open: ALU_OUT, Z
  MUX_10_bit mux_10_bit_2 (
    ._0({10{1'b0}}), ._1(alu_16_bit_1_alu_out[9:0]), .SELECT(bitfinder_1_found), .OUT(NORMALIZED_EXPONENT));

  // Notes on the sheet:
  //   find leading 1
  //   exp (16 bit)
  //   diff (16 bit)
  //   left shift if less than 29
  //   else right shift
endmodule

module Rounder (
  input  [31:0] Normalized_32_bits,
  output [31:0] ROUNDED
);

  wire bitfinder_1_found, n7432_1__3__1y, n7432_1__6__2y;
  wire [0:0] n7408_1__3__1y;
  wire [31:24] alu_32_bit_1_c;

  _7432 u_7432_1 (
    ._1__1A(bitfinder_1_found), ._2__1B(Normalized_32_bits[6]), ._3__1Y(n7432_1__3__1y),
    ._4__2A(n7432_1__3__1y), ._5__2B(Normalized_32_bits[8]), ._6__2Y(n7432_1__6__2y), ._7__GND(1'b0),
    ._14__Vcc(1'b1));  // open: _13__4B, _12__4A, _11__4Y, _10__3B, _9__3A, _8__3Y
  _7408 u_7408_1 (
    ._1__1A(Normalized_32_bits[7]), ._2__1B(n7432_1__6__2y), ._3__1Y(n7408_1__3__1y[0]), ._7__GND(1'b0),
    ._14__Vcc(1'b1));  // open: _4__2A, _5__2B, _6__2Y, _13__4B, _12__4A, _11__4Y, _10__3B, _9__3A, _8__3Y
  BitFinder #(.width(6), .\type ("high1")) bitfinder_1 (
    .in(Normalized_32_bits[5:0]), .found(bitfinder_1_found));  // open: index
  ALU_32_bit alu_32_bit_1 (
    .OpCode({6{1'b0}}), .Invert_B_Signal(1'b0), .A({{8{1'b0}}, Normalized_32_bits[31:8]}),
    .B({{31{1'b0}}, n7408_1__3__1y[0]}), .Cin(1'b0), .C({alu_32_bit_1_c, ROUNDED[31:8]}));  // open: Cout, OVF

  assign ROUNDED[7:0] = {8{1'b0}};

  // Notes on the sheet:
  //   G
  //   S
  //   R
endmodule

module MUX_32_bit (
  input  [31:0] _0,
  input  [31:0] _1,
  input  S,
  output [31:0] out_4
);

  // _74157 74157_1: pin names not known
  _74157 u_74157_2 (
    ._1__S(S), ._2__A1(_0[0]), ._3__B1(_1[0]), ._4__Y1(out_4[0]), ._5__A2(_0[1]), ._6__B2(_1[1]),
    ._7__Y2(out_4[1]), ._15__G(1'b0), ._14__A4(_0[2]), ._13__B4(_1[2]), ._12__Y4(out_4[2]), ._11__A3(_0[3]),
    ._10__B3(_1[3]), ._9__Y3(out_4[3]));  // open: _8__GND, _16__Vcc
  _74157 u_74157_3 (
    ._1__S(S), ._2__A1(_0[4]), ._3__B1(_1[4]), ._4__Y1(out_4[4]), ._5__A2(_0[5]), ._6__B2(_1[5]),
    ._7__Y2(out_4[5]), ._15__G(1'b0), ._14__A4(_0[7]), ._13__B4(_1[7]), ._12__Y4(out_4[7]), ._11__A3(_0[6]),
    ._10__B3(_1[6]), ._9__Y3(out_4[6]));  // open: _8__GND, _16__Vcc
  _74157 u_74157_4 (
    ._1__S(S), ._2__A1(_0[8]), ._3__B1(_1[8]), ._4__Y1(out_4[8]), ._5__A2(_0[9]), ._6__B2(_1[9]),
    ._7__Y2(out_4[9]), ._15__G(1'b0), ._14__A4(_0[11]), ._13__B4(_1[11]), ._12__Y4(out_4[11]),
    ._11__A3(_0[10]), ._10__B3(_1[10]), ._9__Y3(out_4[10]));  // open: _8__GND, _16__Vcc
  _74157 u_74157_5 (
    ._1__S(S), ._2__A1(_0[12]), ._3__B1(_1[12]), ._4__Y1(out_4[12]), ._5__A2(_0[13]), ._6__B2(_1[13]),
    ._7__Y2(out_4[13]), ._15__G(1'b0), ._14__A4(_0[15]), ._13__B4(_1[15]), ._12__Y4(out_4[15]),
    ._11__A3(_0[14]), ._10__B3(_1[14]), ._9__Y3(out_4[14]));  // open: _8__GND, _16__Vcc
  _74157 u_74157_6 (
    ._1__S(S), ._2__A1(_0[16]), ._3__B1(_1[16]), ._4__Y1(out_4[16]), ._5__A2(_0[17]), ._6__B2(_1[17]),
    ._7__Y2(out_4[17]), ._15__G(1'b0), ._14__A4(_0[19]), ._13__B4(_1[19]), ._12__Y4(out_4[19]),
    ._11__A3(_0[18]), ._10__B3(_1[18]), ._9__Y3(out_4[18]));  // open: _8__GND, _16__Vcc
  _74157 u_74157_7 (
    ._1__S(S), ._2__A1(_0[20]), ._3__B1(_1[20]), ._4__Y1(out_4[20]), ._5__A2(_0[21]), ._6__B2(_1[21]),
    ._7__Y2(out_4[21]), ._15__G(1'b0), ._14__A4(_0[23]), ._13__B4(_1[23]), ._12__Y4(out_4[23]),
    ._11__A3(_0[22]), ._10__B3(_1[22]), ._9__Y3(out_4[22]));  // open: _8__GND, _16__Vcc
  _74157 u_74157_8 (
    ._1__S(S), ._2__A1(_0[24]), ._3__B1(_1[24]), ._4__Y1(out_4[24]), ._5__A2(_0[25]), ._6__B2(_1[25]),
    ._7__Y2(out_4[25]), ._15__G(1'b0), ._14__A4(_0[27]), ._13__B4(_1[27]), ._12__Y4(out_4[27]),
    ._11__A3(_0[26]), ._10__B3(_1[26]), ._9__Y3(out_4[26]));  // open: _8__GND, _16__Vcc
  _74157 u_74157_9 (
    ._1__S(S), ._2__A1(_0[28]), ._3__B1(_1[28]), ._4__Y1(out_4[28]), ._5__A2(_0[29]), ._6__B2(_1[29]),
    ._7__Y2(out_4[29]), ._15__G(1'b0), ._14__A4(_0[31]), ._13__B4(_1[31]), ._12__Y4(out_4[31]),
    ._11__A3(_0[30]), ._10__B3(_1[30]), ._9__Y3(out_4[30]));  // open: _8__GND, _16__Vcc
endmodule

module Floating_point_adder (
  input  [31:0] X,
  input  [31:0] Y,
  output [31:0] Out,
  output OVERFLOW,
  output UNDERFLOW
);

  wire comparator_1_x_y, normalizer_1_overflow, normalizer_1_underflow, normalizer_2_overflow,
       normalizer_2_underflow;
  wire [4:0] comparator_1_difference;
  wire [7:0] normalizer_2_normalized_fraction;
  wire [9:0] comparator_1_larger, normalizer_1_normalized_exponent;
  wire [23:21] normalizer_2_normalized_fraction_2;
  wire [30:0] alu_32_bit_1_c;
  wire [31:0] mux_32_bit_1_out_4, mux_32_bit_2_out_4, normalizer_1_normalized_fraction, rounder_1_rounded,
       shifter_1_out, sign_check_1_output, sign_check_2_output, sign_check_3_output;

  Sign_check sign_check_1 (
    .Sign(X[31]), .Fraction({3'b001, X[20:0], {8{1'b0}}}), .Exponent(X[30:21]), .\output (sign_check_1_output));
  comparator comparator_1 (
    .X(X[30:21]), .Y(Y[30:21]), .X_Y(comparator_1_x_y), .LARGER(comparator_1_larger),
    .DIFFERENCE(comparator_1_difference));
  Sign_check sign_check_2 (
    .Sign(Y[31]), .Fraction({3'b001, Y[20:0], {8{1'b0}}}), .Exponent(Y[30:21]), .\output (sign_check_2_output));
  MUX_32_bit mux_32_bit_1 (
    ._0(sign_check_1_output), ._1(sign_check_2_output), .S(comparator_1_x_y), .out_4(mux_32_bit_1_out_4));
  Sign_check sign_check_3 (
    .Sign(Out[31]), .Fraction({Out[31], alu_32_bit_1_c}), .Exponent(10'h1), .\output (sign_check_3_output));
  Normalizer normalizer_1 (
    .Fraction(sign_check_3_output), .Exponent(comparator_1_larger),
    .NORMALIZED_FRACTION(normalizer_1_normalized_fraction),
    .NORMALIZED_EXPONENT(normalizer_1_normalized_exponent), .OVERFLOW(normalizer_1_overflow),
    .UNDERFLOW(normalizer_1_underflow));
  MUX_32_bit mux_32_bit_2 (
    ._0(sign_check_2_output), ._1(sign_check_1_output), .S(comparator_1_x_y), .out_4(mux_32_bit_2_out_4));
  Shifter #(.width(32), .shift("lr")) shifter_1 (
    .in(mux_32_bit_2_out_4), .\dist (comparator_1_difference), .out(shifter_1_out));
  Rounder rounder_1 (.Normalized_32_bits(normalizer_1_normalized_fraction), .ROUNDED(rounder_1_rounded));
  ALU_32_bit alu_32_bit_1 (
    .OpCode({6{1'b0}}), .Invert_B_Signal(1'b0), .A(mux_32_bit_1_out_4), .B(shifter_1_out), .Cin(1'b0),
    .C({Out[31], alu_32_bit_1_c}));  // open: Cout, OVF
  Normalizer normalizer_2 (
    .Fraction(rounder_1_rounded), .Exponent(normalizer_1_normalized_exponent),
    .NORMALIZED_FRACTION({normalizer_2_normalized_fraction_2, Out[20:0], normalizer_2_normalized_fraction}),
    .NORMALIZED_EXPONENT(Out[30:21]), .OVERFLOW(normalizer_2_overflow), .UNDERFLOW(normalizer_2_underflow));
  _7432 u_7432_1 (
    ._1__1A(normalizer_2_overflow), ._2__1B(normalizer_1_overflow), ._3__1Y(OVERFLOW),
    ._4__2A(normalizer_1_underflow), ._5__2B(normalizer_2_underflow), ._6__2Y(UNDERFLOW));  // open: _7__GND, _14__Vcc, _13__4B, _12__4A, _11__4Y, _10__3B, _9__3A, _8__3Y

  // Notes on the sheet:
  //   Compare Exponents
  //   Exponent
  //   Sign check
  //   Sign check
  //   Sign check
  //   32 bit MUX
  //   Larger
  //   32 bit MUX
  //   Normalizer
  //   Smaller
  //   Rounder
  //   Shift Smaller Number Right
  //   Op Code
  //   Normalizer
  //   32 bit ALU
endmodule
