// Logisim project MUX.circ as structural Verilog: 1 circuit, main circuit main
module main (
  input  [23:0] X,
  input  [23:0] Y,
  input  in_3
);

  wire n74157_1__4__y1, n74157_1__7__y2, n74157_1__9__y3, n74157_1__12__y4, n74157_2__4__y1, n74157_2__7__y2,
       n74157_2__9__y3, n74157_2__12__y4, n74157_3__4__y1, n74157_3__7__y2;

  _74157 u_74157_1 (
    ._1__S(in_3), ._2__A1(X[0]), ._3__B1(Y[0]), ._4__Y1(n74157_1__4__y1), ._5__A2(X[1]), ._6__B2(Y[1]),
    ._7__Y2(n74157_1__7__y2), ._15__G(1'b0), ._14__A4(X[2]), ._13__B4(Y[2]), ._12__Y4(n74157_1__12__y4),
    ._11__A3(X[3]), ._10__B3(Y[3]), ._9__Y3(n74157_1__9__y3));  // open: _8__GND, _16__Vcc
  _74157 u_74157_2 (
    ._1__S(in_3), ._2__A1(X[4]), ._3__B1(Y[4]), ._4__Y1(n74157_2__4__y1), ._5__A2(X[5]), ._6__B2(Y[5]),
    ._7__Y2(n74157_2__7__y2), ._15__G(1'b0), ._14__A4(X[7]), ._13__B4(Y[7]), ._12__Y4(n74157_2__12__y4),
    ._11__A3(X[6]), ._10__B3(Y[6]), ._9__Y3(n74157_2__9__y3));  // open: _8__GND, _16__Vcc
  _74157 u_74157_3 (
    ._1__S(in_3), ._2__A1(X[8]), ._3__B1(Y[8]), ._4__Y1(n74157_3__4__y1), ._5__A2(X[9]), ._6__B2(Y[9]),
    ._7__Y2(n74157_3__7__y2), ._15__G(1'b0));  // open: _8__GND, _16__Vcc, _14__A4, _13__B4, _12__Y4, _11__A3, _10__B3, _9__Y3
endmodule
