// Logisim project MUX24.circ as structural Verilog: 1 circuit, main circuit main
module main (
  input  [23:0] X,
  input  [23:0] Y,
  input  S,
  output [23:0] out_4
);

  _74157 u_74157_1 (
    ._1__S(S), ._2__A1(X[0]), ._3__B1(Y[0]), ._4__Y1(out_4[0]), ._5__A2(X[1]), ._6__B2(Y[1]),
    ._7__Y2(out_4[1]), ._15__G(1'b0), ._14__A4(X[2]), ._13__B4(Y[2]), ._12__Y4(out_4[2]), ._11__A3(X[3]),
    ._10__B3(Y[3]), ._9__Y3(out_4[3]));  // open: _8__GND, _16__Vcc
  _74157 u_74157_2 (
    ._1__S(S), ._2__A1(X[4]), ._3__B1(Y[4]), ._4__Y1(out_4[4]), ._5__A2(X[5]), ._6__B2(Y[5]),
    ._7__Y2(out_4[5]), ._15__G(1'b0), ._14__A4(X[7]), ._13__B4(Y[7]), ._12__Y4(out_4[7]), ._11__A3(X[6]),
    ._10__B3(Y[6]), ._9__Y3(out_4[6]));  // open: _8__GND, _16__Vcc
  _74157 u_74157_3 (
    ._1__S(S), ._2__A1(X[8]), ._3__B1(Y[8]), ._4__Y1(out_4[8]), ._5__A2(X[9]), ._6__B2(Y[9]),
    ._7__Y2(out_4[9]), ._15__G(1'b0), ._14__A4(X[11]), ._13__B4(Y[11]), ._12__Y4(out_4[11]), ._11__A3(X[10]),
    ._10__B3(Y[10]), ._9__Y3(out_4[10]));  // open: _8__GND, _16__Vcc
  _74157 u_74157_4 (
    ._1__S(S), ._2__A1(X[12]), ._3__B1(Y[12]), ._4__Y1(out_4[12]), ._5__A2(X[13]), ._6__B2(Y[13]),
    ._7__Y2(out_4[13]), ._15__G(1'b0), ._14__A4(X[15]), ._13__B4(Y[15]), ._12__Y4(out_4[15]),
    ._11__A3(X[14]), ._10__B3(Y[14]), ._9__Y3(out_4[14]));  // open: _8__GND, _16__Vcc
  _74157 u_74157_5 (
    ._1__S(S), ._2__A1(X[16]), ._3__B1(Y[16]), ._4__Y1(out_4[16]), ._5__A2(X[17]), ._6__B2(Y[17]),
    ._7__Y2(out_4[17]), ._15__G(1'b0), ._14__A4(X[19]), ._13__B4(Y[19]), ._12__Y4(out_4[19]),
    ._11__A3(X[18]), ._10__B3(Y[18]), ._9__Y3(out_4[18]));  // open: _8__GND, _16__Vcc
  _74157 u_74157_6 (
    ._1__S(S), ._2__A1(X[20]), ._3__B1(Y[20]), ._4__Y1(out_4[20]), ._5__A2(X[21]), ._6__B2(Y[21]),
    ._7__Y2(out_4[21]), ._15__G(1'b0), ._14__A4(X[23]), ._13__B4(Y[23]), ._12__Y4(out_4[23]),
    ._11__A3(X[22]), ._10__B3(Y[22]), ._9__Y3(out_4[22]));  // open: _8__GND, _16__Vcc
endmodule
