// Logisim project ROUNDER.circ as structural Verilog: 1 circuit, main circuit main
module main (
  input  [23:0] Normalized_24_bits,
  input  [22:0] in_2
);

  wire n7432_1__3__1y, n7432_1__6__2y, undriven;
  wire [0:0] n7408_1__3__1y;

  _7432 u_7432_1 (
    ._1__1A(Normalized_24_bits[0]), ._2__1B(Normalized_24_bits[1]), ._3__1Y(n7432_1__3__1y),
    ._4__2A(n7432_1__3__1y), ._5__2B(Normalized_24_bits[3]), ._6__2Y(n7432_1__6__2y), ._7__GND(1'b0),
    ._14__Vcc(1'b1));  // open: _13__4B, _12__4A, _11__4Y, _10__3B, _9__3A, _8__3Y
  _7408 u_7408_1 (
    ._1__1A(Normalized_24_bits[2]), ._2__1B(n7432_1__6__2y), ._3__1Y(n7408_1__3__1y[0]), ._7__GND(1'b0),
    ._14__Vcc(1'b1));  // open: _4__2A, _5__2B, _6__2Y, _13__4B, _12__4A, _11__4Y, _10__3B, _9__3A, _8__3Y
  Adder #(.width(24)) adder_1 (.cin(1'b0));  // open: a, b, out, cout
  // Probe on undriven

  // Notes on the sheet:
  //   Normalized 24 bits
  //   G
  //   R
  //   S
  //   Rounded 24 bits
endmodule
