// Logisim project 4-bit-MIPS.circ as structural Verilog: 9 circuits, main circuit main
module main (
  input  CLK,
  output [3:0] t0,
  output [3:0] t1,
  output [3:0] t2,
  output [3:0] t3,
  output [3:0] t4
);

  wire control_unit_1_alusrc, control_unit_1_beq, control_unit_1_bneq, control_unit_1_jump,
       control_unit_1_memread, control_unit_1_memtoreg, control_unit_1_memwrite, control_unit_1_regdst,
       control_unit_1_regwrite, n4_bit_alu_1_zero_flag, n7408_1__3__1y, n7408_1__6__2y, n7474_1__5__q1,
       not_1_out, not_2_out, or_1_out;
  wire [2:0] control_unit_1_aluop;
  wire [3:0] data_memory_1_memdata, instruction_memory_1_dst_reg_shamt_addr__immdt__0_3,
       instruction_memory_1_opcode__12_15, instruction_memory_1_src_reg_1__8_11,
       instruction_memory_1_src_reg_2_dst_reg__4_7, multiplexer_2_out, multiplexer_3_out, multiplexer_6_out,
       n4_bit_alu_1_output, register_file_1_read_data_1, register_file_1_read_data_2;
  wire [7:0] adder_1_out, instruction_memory_1_target_jump_address, multiplexer_1_out, multiplexer_4_out,
       multiplexer_5_out, n8_bit_adder_subtractor_1_out_3, n8_bit_d_flip_flop_1_q;

  _8_Bit_D_flip_flop u_8_bit_d_flip_flop_1 (.D(multiplexer_5_out), .CLK(not_1_out), .Q(n8_bit_d_flip_flop_1_q));
  not not_1 (not_1_out, CLK);
  Multiplexer #(.width(8), .enable("false")) multiplexer_1 (
    .in0({8{1'b0}}), .in1(n8_bit_d_flip_flop_1_q), .out(multiplexer_1_out), .sel(n7474_1__5__q1));
  _7474 u_7474_1 (
    ._2__D1(1'b1), ._3__CLK1(CLK), ._5__Q1(n7474_1__5__q1), ._7__GND(1'b0), ._14__Vcc(1'b1));  // open: _1__CLR1, _4__PR1, _6__nQ1, _13__CLR2, _12__D2, _11__CLK2, _10__PR2, _9__Q2, _8__nQ2
  Instruction_Memory instruction_memory_1 (
    .PC(multiplexer_1_out), .Target_Jump_Address(instruction_memory_1_target_jump_address),
    .Dst_Reg_Shamt_Addr__Immdt__0_3(instruction_memory_1_dst_reg_shamt_addr__immdt__0_3),
    .Src_Reg_2_Dst_Reg__4_7(instruction_memory_1_src_reg_2_dst_reg__4_7),
    .Src_Reg_1__8_11(instruction_memory_1_src_reg_1__8_11), .Opcode__12_15(instruction_memory_1_opcode__12_15));
  Adder adder_1 (.a(multiplexer_1_out), .b({8{1'b0}}), .out(adder_1_out), .cin(1'b1));  // open: cout
  Control_Unit control_unit_1 (
    .Opcode(instruction_memory_1_opcode__12_15), .jump(control_unit_1_jump), .RegDst(control_unit_1_regdst),
    .RegWrite(control_unit_1_regwrite), .MemRead(control_unit_1_memread), .MemWrite(control_unit_1_memwrite),
    .MemtoReg(control_unit_1_memtoreg), .beq(control_unit_1_beq), .bneq(control_unit_1_bneq),
    .ALUsrc(control_unit_1_alusrc), .ALUop(control_unit_1_aluop));  // open: out_2
  Multiplexer #(.width(4), .enable("false")) multiplexer_2 (
    .in0(instruction_memory_1_src_reg_2_dst_reg__4_7),
    .in1(instruction_memory_1_dst_reg_shamt_addr__immdt__0_3), .out(multiplexer_2_out),
    .sel(control_unit_1_regdst));
  Register_File register_file_1 (
    .Reg_1_Address(instruction_memory_1_src_reg_1__8_11),
    .Reg_2_Address(instruction_memory_1_src_reg_2_dst_reg__4_7), .Write_Data(multiplexer_6_out),
    .Write_Reg_Address(multiplexer_2_out), .RegWrite(control_unit_1_regwrite), .Clk(CLK),
    .Read_Data_1(register_file_1_read_data_1), .Read_Data_2(register_file_1_read_data_2), .t0(t0), .t1(t1),
    .t2(t2), .t3(t3), .t4(t4));
  _8_bit_adder_subtractor u_8_bit_adder_subtractor_1 (
    .in_1(adder_1_out), .in_2(instruction_memory_1_dst_reg_shamt_addr__immdt__0_3),
    .out_3(n8_bit_adder_subtractor_1_out_3));
  _4_bit_ALU u_4_bit_alu_1 (
    .A(register_file_1_read_data_1), .B(multiplexer_3_out), .ALUOp(control_unit_1_aluop),
    .Output(n4_bit_alu_1_output), .Zero_Flag(n4_bit_alu_1_zero_flag));
  Multiplexer #(.width(4), .enable("false")) multiplexer_3 (
    .in0(register_file_1_read_data_2), .in1(instruction_memory_1_dst_reg_shamt_addr__immdt__0_3),
    .out(multiplexer_3_out), .sel(control_unit_1_alusrc));
  or or_1 (or_1_out, n7408_1__6__2y, n7408_1__3__1y);
  _7408 u_7408_1 (
    ._1__1A(control_unit_1_beq), ._2__1B(n4_bit_alu_1_zero_flag), ._3__1Y(n7408_1__3__1y),
    ._4__2A(control_unit_1_bneq), ._5__2B(not_2_out), ._6__2Y(n7408_1__6__2y));  // open: _7__GND, _14__Vcc, _13__4B, _12__4A, _11__4Y, _10__3B, _9__3A, _8__3Y
  not not_2 (not_2_out, n4_bit_alu_1_zero_flag);
  Multiplexer #(.width(8), .enable("false")) multiplexer_4 (
    .in0(adder_1_out), .in1(n8_bit_adder_subtractor_1_out_3), .out(multiplexer_4_out), .sel(or_1_out));
  Multiplexer #(.width(8), .enable("false")) multiplexer_5 (
    .in0(multiplexer_4_out), .in1(instruction_memory_1_target_jump_address), .out(multiplexer_5_out),
    .sel(control_unit_1_jump));
  Data_Memory data_memory_1 (
    .Address(n4_bit_alu_1_output), .Write_Data(register_file_1_read_data_2),
    .MemWrite(control_unit_1_memwrite), .MemRead(control_unit_1_memread), .CLK(CLK),
    .MemData(data_memory_1_memdata));
  Multiplexer #(.width(4), .enable("false")) multiplexer_6 (
    .in0(n4_bit_alu_1_output), .in1(data_memory_1_memdata), .out(multiplexer_6_out),
    .sel(control_unit_1_memtoreg));

  // Notes on the sheet:
  //   PC
  //   jmp address
endmodule

module Control_Unit (
  input  [3:0] Opcode,
  output [11:0] out_2,
  output jump,
  output RegDst,
  output RegWrite,
  output MemRead,
  output MemWrite,
  output MemtoReg,
  output beq,
  output bneq,
  output ALUsrc,
  output [2:0] ALUop
);

  ROM #(.addrWidth(4), .dataWidth(12)) rom_1 (
    .addr(Opcode), .data({jump, out_2[10:9], MemRead, MemWrite, MemtoReg, beq, bneq, ALUsrc, ALUop}),
    .sel(1'b1));

  assign {out_2[11], out_2[8:0]} = {jump, MemRead, MemWrite, MemtoReg, beq, bneq, ALUsrc, ALUop};
  assign RegDst = out_2[10];
  assign RegWrite = out_2[9];

  // Notes on the sheet:
  //   opcode
  //   contents of rom_1 (hex, n*v repeats v):
  //   601 20a 11 208 21 602 88 20e 603 20b 348 600 20d 209 800 604
  //   Control Output
endmodule

module _4_bit_ALU (
  input  [3:0] A,
  input  [2:0] ALUOp,
  input  [3:0] B,
  output [3:0] Output,
  output Zero_Flag
);

  wire [3:0] adder_1_out, and_1_out, nor_1_out, or_1_out, shifter_1_out, shifter_2_out, subtractor_1_out;

  Adder #(.width(4)) adder_1 (.a(A), .b(B), .out(adder_1_out), .cin(1'b0));  // open: cout
  Subtractor #(.width(4)) subtractor_1 (.a(A), .b(B), .out(subtractor_1_out), .bin(1'b0));  // open: bout
  assign or_1_out = A | B;  // OR_Gate or_1, 4 bits wide
  assign and_1_out = A & B;  // AND_Gate and_1, 4 bits wide
  assign nor_1_out = ~(A | B);  // NOR_Gate nor_1, 4 bits wide
  Shifter #(.width(4)) shifter_1 (.in(A), .\dist (B[1:0]), .out(shifter_1_out));
  Shifter #(.width(4), .shift("lr")) shifter_2 (.in(A), .\dist (B[1:0]), .out(shifter_2_out));
  Multiplexer #(.select(3), .width(4), .enable("false")) multiplexer_1 (
    .in0(adder_1_out), .in1(subtractor_1_out), .in2(or_1_out), .in3(and_1_out), .in4(nor_1_out),
    .in5(shifter_1_out), .in6(shifter_2_out), .in7(4'b0000), .out(Output), .sel(ALUOp));
  nor nor_2 (Zero_Flag, Output[0], Output[1], Output[2], Output[3]);
endmodule

module Register_File (
  input  [3:0] Reg_1_Address,
  input  [3:0] Reg_2_Address,
  input  [3:0] Write_Data,
  input  [3:0] Write_Reg_Address,
  input  RegWrite,
  input  Clk,
  output [3:0] Read_Data_1,
  output [3:0] Read_Data_2,
  output [3:0] t0,
  output [3:0] t1,
  output [3:0] t2,
  output [3:0] t3,
  output [3:0] t4
);

  wire and_1_out, decoder_1_out1, decoder_1_out2, decoder_1_out3, decoder_1_out4, decoder_1_out5,
       decoder_1_out6;
  wire [2:0] multiplexer_1_out;
  wire [3:0] registers_1_o_sp;

  and and_1 (and_1_out, RegWrite, Clk);
  Decoder #(.select(3), .enable("false")) decoder_1 (
    .out1(decoder_1_out1), .out2(decoder_1_out2), .out3(decoder_1_out3), .out4(decoder_1_out4),
    .out5(decoder_1_out5), .out6(decoder_1_out6), .sel(multiplexer_1_out));  // open: out0, out7
  Multiplexer #(.width(3), .enable("false")) multiplexer_1 (
    .in0(3'b000), .in1(Write_Reg_Address[2:0]), .out(multiplexer_1_out), .sel(and_1_out));
  Registers registers_1 (
    .t0(Write_Data), .CLK0(decoder_1_out1), .t1(Write_Data), .CLK1(decoder_1_out2), .t2(Write_Data),
    .CLK2(decoder_1_out3), .t3(Write_Data), .CLK3(decoder_1_out4), .t4(Write_Data), .CLK4(decoder_1_out5),
    .sp(Write_Data), .CLKSP(decoder_1_out6), .O_t0(t0), .O_t1(t1), .O_t2(t2), .O_t3(t3), .O_t4(t4),
    .O_sp(registers_1_o_sp));
  Multiplexer #(.select(3), .width(4), .disabled(0), .enable("false")) multiplexer_2 (
    .in0(4'b0000), .in1(t0), .in2(t1), .in3(t2), .in4(t3), .in5(t4), .in6(registers_1_o_sp),
    .out(Read_Data_1), .sel(Reg_1_Address[2:0]));  // open: in7
  Multiplexer #(.select(3), .width(4), .disabled(0), .enable("false")) multiplexer_3 (
    .in0(4'b0000), .in1(t0), .in2(t1), .in3(t2), .in4(t3), .in5(t4), .in6(registers_1_o_sp),
    .out(Read_Data_2), .sel(Reg_2_Address[2:0]));  // open: in7

  // Notes on the sheet:
  //   $sp
  //   $t2
  //   $t3
  //   $t4
  //   $t0
  //   $t1
  //   $zero
endmodule

module Instruction_Memory (
  input  [7:0] PC,
  output [7:0] Target_Jump_Address,
  output [3:0] Dst_Reg_Shamt_Addr__Immdt__0_3,
  output [3:0] Src_Reg_2_Dst_Reg__4_7,
  output [3:0] Src_Reg_1__8_11,
  output [3:0] Opcode__12_15
);

  ROM #(.dataWidth(16)) rom_1 (
    .addr(PC), .data({Opcode__12_15, Src_Reg_1__8_11, Src_Reg_2_Dst_Reg__4_7, Dst_Reg_Shamt_Addr__Immdt__0_3}));  // open: sel

  assign Target_Jump_Address = {Src_Reg_1__8_11, Src_Reg_2_Dst_Reg__4_7};

  // Notes on the sheet:
  //   contents of rom_1 (hex, n*v repeats v):
  //   3023 d03e b231 234 f135 6323 7331 4431 e120 c441 a334 e110 5131 9531 1225 8352 e120 231a
endmodule

module Data_Memory (
  input  [3:0] Address,
  input  [3:0] Write_Data,
  input  MemWrite,
  input  MemRead,
  input  CLK,
  output [3:0] MemData
);

  RAM #(.addrWidth(4), .dataWidth(4), .bus("separate")) ram_1 (
    .addr(Address), .din(Write_Data), .data(MemData), .str(MemWrite), .clk(CLK), .ld(MemRead));  // open: sel, clr
endmodule

module Registers (
  input  [3:0] t0,
  input  CLK0,
  input  [3:0] t1,
  input  CLK1,
  input  [3:0] t2,
  input  CLK2,
  input  [3:0] t3,
  input  CLK3,
  input  [3:0] t4,
  input  CLK4,
  input  [3:0] sp,
  input  CLKSP,
  output [3:0] O_t0,
  output [3:0] O_t1,
  output [3:0] O_t2,
  output [3:0] O_t3,
  output [3:0] O_t4,
  output [3:0] O_sp
);

  _7474 u_7474_1 (
    ._2__D1(t0[0]), ._3__CLK1(CLK0), ._5__Q1(O_t0[0]), ._12__D2(t0[1]), ._11__CLK2(CLK0), ._9__Q2(O_t0[1]));  // open: _1__CLR1, _4__PR1, _6__nQ1, _7__GND, _14__Vcc, _13__CLR2, _10__PR2, _8__nQ2
  _7474 u_7474_2 (
    ._2__D1(t0[2]), ._3__CLK1(CLK0), ._5__Q1(O_t0[2]), ._12__D2(t0[3]), ._11__CLK2(CLK0), ._9__Q2(O_t0[3]));  // open: _1__CLR1, _4__PR1, _6__nQ1, _7__GND, _14__Vcc, _13__CLR2, _10__PR2, _8__nQ2
  _7474 u_7474_3 (
    ._2__D1(t1[0]), ._3__CLK1(CLK1), ._5__Q1(O_t1[0]), ._12__D2(t1[1]), ._11__CLK2(CLK1), ._9__Q2(O_t1[1]));  // open: _1__CLR1, _4__PR1, _6__nQ1, _7__GND, _14__Vcc, _13__CLR2, _10__PR2, _8__nQ2
  _7474 u_7474_4 (
    ._2__D1(t1[2]), ._3__CLK1(CLK1), ._5__Q1(O_t1[2]), ._12__D2(t1[3]), ._11__CLK2(CLK1), ._9__Q2(O_t1[3]));  // open: _1__CLR1, _4__PR1, _6__nQ1, _7__GND, _14__Vcc, _13__CLR2, _10__PR2, _8__nQ2
  _7474 u_7474_5 (
    ._2__D1(t2[0]), ._3__CLK1(CLK2), ._5__Q1(O_t2[0]), ._12__D2(t2[1]), ._11__CLK2(CLK2), ._9__Q2(O_t2[1]));  // open: _1__CLR1, _4__PR1, _6__nQ1, _7__GND, _14__Vcc, _13__CLR2, _10__PR2, _8__nQ2
  _7474 u_7474_6 (
    ._2__D1(t2[2]), ._3__CLK1(CLK2), ._5__Q1(O_t2[2]), ._12__D2(t2[3]), ._11__CLK2(CLK2), ._9__Q2(O_t2[3]));  // open: _1__CLR1, _4__PR1, _6__nQ1, _7__GND, _14__Vcc, _13__CLR2, _10__PR2, _8__nQ2
  _7474 u_7474_7 (
    ._2__D1(t3[0]), ._3__CLK1(CLK3), ._5__Q1(O_t3[0]), ._12__D2(t3[1]), ._11__CLK2(CLK3), ._9__Q2(O_t3[1]));  // open: _1__CLR1, _4__PR1, _6__nQ1, _7__GND, _14__Vcc, _13__CLR2, _10__PR2, _8__nQ2
  _7474 u_7474_8 (
    ._2__D1(t3[2]), ._3__CLK1(CLK3), ._5__Q1(O_t3[2]), ._12__D2(t3[3]), ._11__CLK2(CLK3), ._9__Q2(O_t3[3]));  // open: _1__CLR1, _4__PR1, _6__nQ1, _7__GND, _14__Vcc, _13__CLR2, _10__PR2, _8__nQ2
  _7474 u_7474_9 (
    ._2__D1(t4[0]), ._3__CLK1(CLK4), ._5__Q1(O_t4[0]), ._12__D2(t4[1]), ._11__CLK2(CLK4), ._9__Q2(O_t4[1]));  // open: _1__CLR1, _4__PR1, _6__nQ1, _7__GND, _14__Vcc, _13__CLR2, _10__PR2, _8__nQ2
  _7474 u_7474_10 (
    ._2__D1(t4[2]), ._3__CLK1(CLK4), ._5__Q1(O_t4[2]), ._12__D2(t4[3]), ._11__CLK2(CLK4), ._9__Q2(O_t4[3]));  // open: _1__CLR1, _4__PR1, _6__nQ1, _7__GND, _14__Vcc, _13__CLR2, _10__PR2, _8__nQ2
  _7474 u_7474_11 (
    ._2__D1(sp[0]), ._3__CLK1(CLKSP), ._5__Q1(O_sp[0]), ._12__D2(sp[1]), ._11__CLK2(CLKSP), ._9__Q2(O_sp[1]));  // open: _1__CLR1, _4__PR1, _6__nQ1, _7__GND, _14__Vcc, _13__CLR2, _10__PR2, _8__nQ2
  _7474 u_7474_12 (
    ._2__D1(sp[2]), ._3__CLK1(CLKSP), ._5__Q1(O_sp[2]), ._12__D2(sp[3]), ._11__CLK2(CLKSP), ._9__Q2(O_sp[3]));  // open: _1__CLR1, _4__PR1, _6__nQ1, _7__GND, _14__Vcc, _13__CLR2, _10__PR2, _8__nQ2
endmodule

module _8_Bit_D_flip_flop (
  input  [7:0] D,
  input  CLK,
  output [7:0] Q
);

  _7474 u_7474_1 (
    ._2__D1(D[0]), ._3__CLK1(CLK), ._5__Q1(Q[0]), ._12__D2(D[1]), ._11__CLK2(CLK), ._9__Q2(Q[1]));  // open: _1__CLR1, _4__PR1, _6__nQ1, _7__GND, _14__Vcc, _13__CLR2, _10__PR2, _8__nQ2
  _7474 u_7474_2 (
    ._2__D1(D[2]), ._3__CLK1(CLK), ._5__Q1(Q[2]), ._12__D2(D[3]), ._11__CLK2(CLK), ._9__Q2(Q[3]));  // open: _1__CLR1, _4__PR1, _6__nQ1, _7__GND, _14__Vcc, _13__CLR2, _10__PR2, _8__nQ2
  _7474 u_7474_3 (
    ._2__D1(D[4]), ._3__CLK1(CLK), ._5__Q1(Q[4]), ._12__D2(D[5]), ._11__CLK2(CLK), ._9__Q2(Q[5]));  // open: _1__CLR1, _4__PR1, _6__nQ1, _7__GND, _14__Vcc, _13__CLR2, _10__PR2, _8__nQ2
  _7474 u_7474_4 (
    ._2__D1(D[6]), ._3__CLK1(CLK), ._5__Q1(Q[6]), ._12__D2(D[7]), ._11__CLK2(CLK), ._9__Q2(Q[7]));  // open: _1__CLR1, _4__PR1, _6__nQ1, _7__GND, _14__Vcc, _13__CLR2, _10__PR2, _8__nQ2
endmodule

module _8_bit_adder_subtractor (
  input  [7:0] in_1,
  input  [3:0] in_2,
  output [7:0] out_3
);

  wire [7:0] adder_1_out, negator_1_out, subtractor_1_out;

  Negator negator_1 (.in({{5{in_2[3]}}, in_2[2:0]}), .out(negator_1_out));
  Adder adder_1 (.a(in_1), .b({{5{in_2[3]}}, in_2[2:0]}), .out(adder_1_out));  // open: cin, cout
  Subtractor subtractor_1 (.a(in_1), .b(negator_1_out), .out(subtractor_1_out));  // open: bin, bout
  Multiplexer #(.width(8), .enable("false")) multiplexer_1 (
    .in0(adder_1_out), .in1(subtractor_1_out), .out(out_3), .sel(in_2[3]));
endmodule
